# Fritzing sketch Untitled Sketch 2 (saved by Fritzing 0.8.5b)
circuit board: 5.9615cm x 3.90548cm
breadboards: 1

parts:
  Part1 = Arduino Nano (Rev3.0)
  C1 = Electrolytic Capacitor [capacitance=100µF package="200 mil [THT, electrolytic]"]
  J1 = female pin header, 2 pins [form="♀ (female)"]
  J2 = female pin header, 3 pins [form="♀ (female)"]
  J3 = female pin header, 3 pins [form="♀ (female)"]
  J4 = female pin header, 3 pins [form="♀ (female)"]
  J5 = female pin header, 3 pins [form="♀ (female)"]

nets:
  N1: Part1.GND, C1.-, J1.pin1, J2.pin1, J3.pin1, J4.pin1, J5.pin1
  N2: Part1.D6, J3.pin3
  N3: Part1.D9, J5.pin3
  N4: Part1.D10, J4.pin3
  N5: Part1.D11/MOSI, J2.pin3
  N6: C1.+, J1.pin2, J2.pin2, J3.pin2, J4.pin2, J5.pin2
